# Fritzing sketch Curso_Programacion-Montaje (saved by Fritzing 0.9.3b)
breadboards: 1

parts:
  Componente1 = Arduino Uno (Rev3)
  S1 = Pushbutton [package="[SMD]"]
  S2 = Pushbutton [package="[THT]"]
  R1 = Resistor [tolerance=±5% resistance=10k package=THT]
  LED1 = LED - 5mm [color="Red (633nm)" package="5 mm [THT]"]
  LED2 = LED - 5mm [color="Red (633nm)" package="5 mm [THT]"]
  LED3 = LED - 5mm [color="Red (633nm)" package="5 mm [THT]"]
  LED4 = LED - 5mm [color="Red (633nm)" package="5 mm [THT]"]
  R2 = Resistor [tolerance=±5% resistance=220 package=THT]
  R3 = Resistor [tolerance=±5% resistance=220 package=THT]
  R4 = Resistor [tolerance=±5% resistance=220 package=THT]
  R5 = Resistor [tolerance=±5% resistance=220 package=THT]
  R6 = Rotary Potentiometer (Small) [maximum_resistance=100kΩ package=THT]
  J1 = Basic Servo
  R7 = Photocell (LDR) [package=THT]
  R8 = Resistor [tolerance=±5% resistance=10k package=THT]
  J2 = Piezo Speaker
  U1 = TMP36 [package=to-92]

nets:
  N1: Componente1.A0, R6.wiper
  N2: Componente1.A1, R7.pin_1, R8.Pin_0
  N3: Componente1.A2, U1.VOUT
  N4: Componente1.D8, J2.pin2
  N5: Componente1.D9_PWM, J1.pulse
  N6: Componente1.D2, S1.Pin_1, S1.Pin_2
  N7: Componente1.D3_PWM, S2.Pin_3, S2.Pin_4, R1.Pin_1
  N8: Componente1.D4, LED4.anode
  N9: Componente1.D5_PWM, LED3.anode
  N10: Componente1.D6_PWM, LED2.anode
  N11: Componente1.D7, LED1.anode
  VCC: Componente1.5V, S2.Pin_1, S2.Pin_2, R6.leg2, J1.vcc, R7.pin_0, U1.VCC
  GND: Componente1.GND, S1.Pin_3, S1.Pin_4, R1.Pin_0, R2.Pin_1, R3.Pin_1, R4.Pin_1, R5.Pin_1, R6.leg1, J1.gnd, R8.Pin_1, J2.pin1, U1.GND
  N12: LED1.cathode, R2.Pin_0
  N13: LED2.cathode, R3.Pin_0
  N14: LED3.cathode, R4.Pin_0
  N15: LED4.cathode, R5.Pin_0
